# Fritzing sketch mosquito_lamp_final (saved by Fritzing 0.9.3b)

parts:
  Mod1 = KY-019 5V Relay Module [package="Breakout board"]
  DHT11_1 = DHT11 module
  A1 = USB power module
  Mod2 = ESP32 - CAM

nets:
  N1: Mod1.S, Mod2.IO12
  N2: Mod1.+, Mod2.IO4
  GND: Mod1.-, DHT11_1.GND, A1.Pin_4, Mod2.GND
  N3: Mod1.Common, A1.Pin_1, A1.Pin_3, Mod2.3V3
  VCC: DHT11_1.VCC, Mod2.VCC
  N4: DHT11_1.DATA, Mod2.IO2

custom parts:
  KY-019 5V Relay Module: KY-019 5V Relay module, used to control AC circuits. (Special thanks to vanepp for fixing the PCB holes and other errors)
  DHT11 module: https://cdn-learn.adafruit.com/downloads/pdf/dht.pdf DHT11 black pcb module reference by:https://github.com/adafruit/Fritzing-Library/blob/master/parts/DHT11%20Humitidy%20and%20Temperature%20Sensor.fzpz
  USB power module: PD QC AFC Fast Charge Decoy Trigger Module USB-PWR Module Supports 5V 9V 12V 15V 20V Fixed Voltage Output.
  ESP32 - CAM: The ESP32-CAM has a very competitive small-size camera module that can operate independently as a minimum system with a footprint of only 27*40.5*4.5mm and a deep sleep current of up to 6mA.
